// Logisim project Блоки.circ as structural Verilog: 4 circuits, main circuit REGISTER
module ADDER (
  input  [3:0] TERM_0,
  input  [3:0] TERM_1,
  input  CARRY_IN,
  output [3:0] RESULT,
  output CARRY_OUT
);

  wire full_summator_1_carry_out, full_summator_2_carry_out, full_summator_3_carry_out;

  FULL_SUMMATOR full_summator_1 (
    .A_BIT(TERM_0[0]), .B_BIT(TERM_1[0]), .CARRY_IN(CARRY_IN), .RESULT(RESULT[0]),
    .CARRY_OUT(full_summator_1_carry_out));
  FULL_SUMMATOR full_summator_2 (
    .A_BIT(TERM_0[1]), .B_BIT(TERM_1[1]), .CARRY_IN(full_summator_1_carry_out), .RESULT(RESULT[1]),
    .CARRY_OUT(full_summator_2_carry_out));
  FULL_SUMMATOR full_summator_3 (
    .A_BIT(TERM_0[2]), .B_BIT(TERM_1[2]), .CARRY_IN(full_summator_2_carry_out), .RESULT(RESULT[2]),
    .CARRY_OUT(full_summator_3_carry_out));
  FULL_SUMMATOR full_summator_4 (
    .A_BIT(TERM_0[3]), .B_BIT(TERM_1[3]), .CARRY_IN(full_summator_3_carry_out), .RESULT(RESULT[3]),
    .CARRY_OUT(CARRY_OUT));
endmodule

module SUBTRACTOR (
  input  [3:0] TERM_0,
  input  [3:0] TERM_1,
  input  BORROW_IN,
  output [3:0] RESULT,
  output BORROW_OUT
);

  wire full_substractor_1_borrow_out, full_substractor_2_borrow_out, full_substractor_3_borrow_out;

  FULL_SUBSTRACTOR full_substractor_1 (
    .A_BIT(TERM_0[0]), .B_BIT(TERM_1[0]), .BORROW_IN(BORROW_IN), .RESULT(RESULT[0]),
    .BORROW_OUT(full_substractor_1_borrow_out));
  FULL_SUBSTRACTOR full_substractor_2 (
    .A_BIT(TERM_0[1]), .B_BIT(TERM_1[1]), .BORROW_IN(full_substractor_1_borrow_out), .RESULT(RESULT[1]),
    .BORROW_OUT(full_substractor_2_borrow_out));
  FULL_SUBSTRACTOR full_substractor_3 (
    .A_BIT(TERM_0[2]), .B_BIT(TERM_1[2]), .BORROW_IN(full_substractor_2_borrow_out), .RESULT(RESULT[2]),
    .BORROW_OUT(full_substractor_3_borrow_out));
  FULL_SUBSTRACTOR full_substractor_4 (
    .A_BIT(TERM_0[3]), .B_BIT(TERM_1[3]), .BORROW_IN(full_substractor_3_borrow_out), .RESULT(RESULT[3]),
    .BORROW_OUT(BORROW_OUT));
endmodule

module REGISTER (
  input  [3:0] DATA,
  input  CLK,
  output [3:0] RESULT
);

  D_TRIGGER d_trigger_1 (.DATA(DATA[0]), .CLK(CLK), .RESULT(RESULT[0]));  // open: NOT_RESULT
  D_TRIGGER d_trigger_2 (.DATA(DATA[1]), .CLK(CLK), .RESULT(RESULT[1]));  // open: NOT_RESULT
  D_TRIGGER d_trigger_3 (.DATA(DATA[2]), .CLK(CLK), .RESULT(RESULT[2]));  // open: NOT_RESULT
  D_TRIGGER d_trigger_4 (.DATA(DATA[3]), .CLK(CLK), .RESULT(RESULT[3]));  // open: NOT_RESULT
endmodule

module SHIFTER (
  input  [3:0] DATA,
  input  LEFT,
  input  LOOP,
  output [3:0] RESULT
);

  wire and_1_out, and_2_out;

  and and_1 (and_1_out, DATA[0], LOOP);
  and and_2 (and_2_out, DATA[3], LOOP);
  MUXER_2_TO_1 muxer_2_to_1_1 (.IN_0(DATA[1]), .IN_1(and_2_out), .OUT(RESULT[0]), .SELECT(LEFT));
  MUXER_2_TO_1 muxer_2_to_1_2 (.IN_0(DATA[2]), .IN_1(DATA[0]), .OUT(RESULT[1]), .SELECT(LEFT));
  MUXER_2_TO_1 muxer_2_to_1_3 (.IN_0(DATA[3]), .IN_1(DATA[1]), .OUT(RESULT[2]), .SELECT(LEFT));
  MUXER_2_TO_1 muxer_2_to_1_4 (.IN_0(and_1_out), .IN_1(DATA[2]), .OUT(RESULT[3]), .SELECT(LEFT));
endmodule
