// Logisim project Примитивы.circ as structural Verilog: 23 circuits, main circuit HALF_SUMMATOR
module HALF_SUMMATOR (
  input  A_BIT,
  input  B_BIT,
  output RESULT,
  output CARRY
);

  xor xor_1 (RESULT, A_BIT, B_BIT);
  and and_1 (CARRY, B_BIT, A_BIT);
endmodule

module FULL_SUMMATOR (
  input  A_BIT,
  input  B_BIT,
  input  CARRY_IN,
  output RESULT,
  output CARRY_OUT
);

  wire and_1_out, and_2_out, xor_1_out;

  xor xor_1 (xor_1_out, A_BIT, B_BIT);
  xor xor_2 (RESULT, xor_1_out, CARRY_IN);
  and and_1 (and_1_out, xor_1_out, CARRY_IN);
  and and_2 (and_2_out, A_BIT, B_BIT);
  or or_1 (CARRY_OUT, and_1_out, and_2_out);
endmodule

module HALF_SUBSTRACTOR (
  input  A_BIT,
  input  B_BIT,
  output RESULT,
  output BORROW
);

  wire not_1_out;

  not not_1 (not_1_out, A_BIT);
  and and_1 (BORROW, B_BIT, not_1_out);
  xor xor_1 (RESULT, A_BIT, B_BIT);
endmodule

module FULL_SUBSTRACTOR (
  input  A_BIT,
  input  B_BIT,
  input  BORROW_IN,
  output RESULT,
  output BORROW_OUT
);

  wire and_1_out, and_2_out, not_1_out, not_2_out, xor_1_out;

  xor xor_1 (xor_1_out, A_BIT, B_BIT);
  not not_1 (not_1_out, A_BIT);
  and and_1 (and_1_out, not_1_out, B_BIT);
  xor xor_2 (RESULT, xor_1_out, BORROW_IN);
  not not_2 (not_2_out, xor_1_out);
  and and_2 (and_2_out, BORROW_IN, not_2_out);
  or or_1 (BORROW_OUT, and_2_out, and_1_out);
endmodule

module MULTIPLIER (
  input  A_BIT,
  input  B_BIT,
  output RESULT
);

  and and_1 (RESULT, A_BIT, B_BIT);
endmodule

module DIVIDER (
  input  A_BIT,
  input  B_BIT,
  output RESULT,
  output ERROR
);

  and and_1 (RESULT, A_BIT, B_BIT);
  not not_1 (ERROR, B_BIT);
endmodule

module COMPARATOR (
  input  A_BIT,
  input  B_BIT,
  output MORE,
  output EQUAL,
  output LESS
);

  wire not_1_out, not_2_out, or_1_out;

  not not_1 (not_1_out, B_BIT);
  not not_2 (not_2_out, A_BIT);
  and and_1 (MORE, A_BIT, not_1_out);
  and and_2 (LESS, not_2_out, B_BIT);
  or or_1 (or_1_out, MORE, LESS);
  not not_3 (EQUAL, or_1_out);
endmodule

module RS_TRIGGER (
  input  SET,
  input  RESET,
  output NOT_RESULT,
  output RESULT
);

  nor nor_1 (NOT_RESULT, SET, RESULT);
  nor nor_2 (RESULT, NOT_RESULT, RESET);
endmodule

module D_TRIGGER (
  input  DATA,
  input  CLK,
  output RESULT,
  output NOT_RESULT
);

  wire nand_1_out, nand_2_out;

  nand nand_1 (nand_1_out, DATA, CLK);
  nand nand_2 (nand_2_out, nand_1_out, CLK);
  nand nand_3 (RESULT, nand_1_out, NOT_RESULT);
  nand nand_4 (NOT_RESULT, RESULT, nand_2_out);
endmodule

module JK_TRIGGER (
  input  J_SET,
  input  CLK,
  input  K_RESET,
  output RESULT,
  output NOT_RESULT
);

  wire nand_1_out, nand_2_out;

  nand nand_1 (nand_1_out, J_SET, CLK, NOT_RESULT);
  nand nand_2 (nand_2_out, RESULT, CLK, K_RESET);
  nand nand_3 (RESULT, nand_1_out, NOT_RESULT);
  nand nand_4 (NOT_RESULT, RESULT, nand_2_out);
endmodule

module T_TRIGGER (
  input  TOGGLE,
  input  CLK,
  output RESULT,
  output NOT_RESULT
);

  wire nand_1_out, nand_2_out;

  nand nand_1 (nand_1_out, NOT_RESULT, TOGGLE, CLK);
  nand nand_2 (nand_2_out, CLK, TOGGLE, RESULT);
  nor nor_1 (RESULT, nand_1_out, NOT_RESULT);
  nor nor_2 (NOT_RESULT, RESULT, nand_2_out);
endmodule

module DECODER_1_TO_2 (
  input  Y_0,
  output X_0,
  output X_1
);

  not not_1 (X_0, Y_0);

  assign X_1 = Y_0;
endmodule

module DECODER_2_TO_4 (
  input  Y_0,
  input  Y_1,
  output X_0,
  output X_1,
  output X_2,
  output X_3
);

  wire not_1_out, not_2_out;

  not not_1 (not_1_out, Y_0);
  not not_2 (not_2_out, Y_1);
  and and_1 (X_0, not_1_out, not_2_out);
  and and_2 (X_1, Y_0, not_2_out);
  and and_3 (X_2, not_1_out, Y_1);
  and and_4 (X_3, Y_0, Y_1);
endmodule

module DECODER_3_TO_8 (
  input  Y_0,
  input  Y_1,
  input  Y_2,
  output X_0,
  output X_1,
  output X_2,
  output X_3,
  output X_4,
  output X_5,
  output X_6,
  output X_7
);

  wire not_1_out, not_2_out, not_3_out;

  not not_1 (not_1_out, Y_0);
  not not_2 (not_2_out, Y_1);
  not not_3 (not_3_out, Y_2);
  and and_1 (X_0, not_1_out, not_2_out, not_3_out);
  and and_2 (X_1, Y_0, not_2_out, not_3_out);
  and and_3 (X_2, not_1_out, Y_1, not_3_out);
  and and_4 (X_3, Y_0, Y_1, not_3_out);
  and and_5 (X_4, not_1_out, not_2_out, Y_2);
  and and_6 (X_5, Y_0, not_2_out, Y_2);
  and and_7 (X_6, not_1_out, Y_1, Y_2);
  and and_8 (X_7, Y_0, Y_1, Y_2);
endmodule

module ENCODER_2_TO_1 (
  input  X_0,
  input  X_1,
  output Y_0
);


  assign Y_0 = X_1;
endmodule

module ENCODER_4_TO_2 (
  input  X_0,
  input  X_1,
  input  X_2,
  input  X_3,
  output Y_0,
  output Y_1
);

  or or_1 (Y_0, X_1, X_3);
  or or_2 (Y_1, X_2, X_3);
endmodule

module ENCODER_8_TO_3 (
  input  X_0,
  input  X_1,
  input  X_2,
  input  X_3,
  input  X_4,
  input  X_5,
  input  X_6,
  input  X_7,
  output Y_0,
  output Y_1,
  output Y_2
);

  or or_1 (Y_0, X_1, X_3, X_5, X_7);
  or or_2 (Y_1, X_2, X_3, X_7, X_6);
  or or_3 (Y_2, X_5, X_4, X_6, X_7);
endmodule

module MUXER_2_TO_1 (
  input  SELECT,
  input  IN_0,
  input  IN_1,
  output OUT
);

  wire and_1_out, and_2_out, not_1_out;

  not not_1 (not_1_out, SELECT);
  and and_1 (and_1_out, IN_0, not_1_out);
  and and_2 (and_2_out, IN_1, SELECT);
  or or_1 (OUT, and_1_out, and_2_out);
endmodule

module MUXER_4_TO_1 (
  input  SELECT_0,
  input  SELECT_1,
  input  IN_0,
  input  IN_1,
  input  IN_2,
  input  IN_3,
  output OUT
);

  wire and_1_out, and_2_out, and_3_out, and_4_out, not_1_out, not_2_out;

  not not_1 (not_1_out, SELECT_0);
  not not_2 (not_2_out, SELECT_1);
  and and_1 (and_1_out, IN_0, not_2_out, not_1_out);
  and and_2 (and_2_out, IN_1, SELECT_0, not_2_out);
  and and_3 (and_3_out, IN_2, SELECT_1, not_1_out);
  and and_4 (and_4_out, IN_3, SELECT_1, SELECT_0);
  or or_1 (OUT, and_1_out, and_2_out, and_3_out, and_4_out);
endmodule

module MUXER_8_TO_1 (
  input  SELECT_0,
  input  SELECT_1,
  input  SELECT_2,
  input  IN_0,
  input  IN_1,
  input  IN_2,
  input  IN_3,
  input  IN_4,
  input  IN_5,
  input  IN_6,
  input  IN_7,
  output OUT
);

  wire and_1_out, and_2_out, and_3_out, and_4_out, and_5_out, and_6_out, and_7_out, and_8_out, not_1_out,
       not_2_out, not_3_out;

  not not_1 (not_1_out, SELECT_0);
  not not_2 (not_2_out, SELECT_1);
  not not_3 (not_3_out, SELECT_2);
  and and_1 (and_1_out, IN_0, not_3_out, not_2_out, not_1_out);
  and and_2 (and_2_out, IN_1, not_3_out, not_2_out, SELECT_0);
  and and_3 (and_3_out, IN_2, not_3_out, SELECT_1, not_1_out);
  and and_4 (and_4_out, IN_3, not_3_out, SELECT_1, SELECT_0);
  and and_5 (and_5_out, IN_4, SELECT_2, not_2_out, not_1_out);
  and and_6 (and_6_out, IN_5, SELECT_2, not_2_out, SELECT_0);
  and and_7 (and_7_out, IN_6, SELECT_2, SELECT_1, not_1_out);
  and and_8 (and_8_out, IN_7, SELECT_2, SELECT_1, SELECT_0);
  or or_1 (OUT, and_1_out, and_2_out, and_3_out, and_4_out, and_5_out, and_6_out, and_7_out, and_8_out);
endmodule

module DEMUXER_1_TO_2 (
  input  SELECT,
  input  IN,
  output OUT_0,
  output OUT_1
);

  wire not_1_out;

  not not_1 (not_1_out, SELECT);
  and and_1 (OUT_0, IN, not_1_out);
  and and_2 (OUT_1, IN, SELECT);
endmodule

module DEMUXER_1_TO_4 (
  input  SELECT_0,
  input  SELECT_1,
  input  IN,
  output OUT_0,
  output OUT_1,
  output OUT_2,
  output OUT_3
);

  wire not_1_out, not_2_out;

  not not_1 (not_1_out, SELECT_0);
  not not_2 (not_2_out, SELECT_1);
  and and_1 (OUT_0, IN, not_2_out, not_1_out);
  and and_2 (OUT_1, IN, not_2_out, SELECT_0);
  and and_3 (OUT_2, IN, SELECT_1, not_1_out);
  and and_4 (OUT_3, IN, SELECT_1, SELECT_0);
endmodule

module DEMUXER_1_TO_8 (
  input  SELECT_0,
  input  SELECT_1,
  input  SELECT_2,
  input  IN,
  output OUT_0,
  output OUT_1,
  output OUT_2,
  output OUT_3,
  output OUT_4,
  output OUT_5,
  output OUT_6,
  output OUT_7
);

  wire not_1_out, not_2_out, not_3_out;

  not not_1 (not_1_out, SELECT_0);
  not not_2 (not_2_out, SELECT_1);
  not not_3 (not_3_out, SELECT_2);
  and and_1 (OUT_0, IN, not_3_out, not_2_out, not_1_out);
  and and_2 (OUT_1, IN, not_3_out, not_2_out, SELECT_0);
  and and_3 (OUT_2, IN, not_3_out, SELECT_1, not_1_out);
  and and_4 (OUT_3, IN, not_3_out, SELECT_1, SELECT_0);
  and and_5 (OUT_4, IN, SELECT_2, not_2_out, not_1_out);
  and and_6 (OUT_5, IN, SELECT_2, not_2_out, SELECT_0);
  and and_7 (OUT_6, IN, SELECT_2, SELECT_1, not_1_out);
  and and_8 (OUT_7, IN, SELECT_2, SELECT_1, SELECT_0);
endmodule
