// Logisim project Блоки.circ as structural Verilog: 7 circuits, main circuit REGISTER
module SUMMATOR (
  input  [3:0] TERM_0,
  input  [3:0] TERM_1,
  input  CARRY_IN,
  output [3:0] RESULT,
  output CARRY_OUT
);

  wire full_summator_1_carry_out, full_summator_2_carry_out, full_summator_3_carry_out;

  FULL_SUMMATOR full_summator_1 (
    .A_BIT(TERM_0[0]), .B_BIT(TERM_1[0]), .CARRY_IN(CARRY_IN), .RESULT(RESULT[0]),
    .CARRY_OUT(full_summator_1_carry_out));
  FULL_SUMMATOR full_summator_2 (
    .A_BIT(TERM_0[1]), .B_BIT(TERM_1[1]), .CARRY_IN(full_summator_1_carry_out), .RESULT(RESULT[1]),
    .CARRY_OUT(full_summator_2_carry_out));
  FULL_SUMMATOR full_summator_3 (
    .A_BIT(TERM_0[2]), .B_BIT(TERM_1[2]), .CARRY_IN(full_summator_2_carry_out), .RESULT(RESULT[2]),
    .CARRY_OUT(full_summator_3_carry_out));
  FULL_SUMMATOR full_summator_4 (
    .A_BIT(TERM_0[3]), .B_BIT(TERM_1[3]), .CARRY_IN(full_summator_3_carry_out), .RESULT(RESULT[3]),
    .CARRY_OUT(CARRY_OUT));
endmodule

module SUBTRACTOR (
  input  [3:0] TERM_0,
  input  [3:0] TERM_1,
  input  BORROW_IN,
  output [3:0] RESULT,
  output BORROW_OUT
);

  wire full_substractor_1_borrow_out, full_substractor_2_borrow_out, full_substractor_3_borrow_out;

  FULL_SUBSTRACTOR full_substractor_1 (
    .A_BIT(TERM_0[0]), .B_BIT(TERM_1[0]), .BORROW_IN(BORROW_IN), .RESULT(RESULT[0]),
    .BORROW_OUT(full_substractor_1_borrow_out));
  FULL_SUBSTRACTOR full_substractor_2 (
    .A_BIT(TERM_0[1]), .B_BIT(TERM_1[1]), .BORROW_IN(full_substractor_1_borrow_out), .RESULT(RESULT[1]),
    .BORROW_OUT(full_substractor_2_borrow_out));
  FULL_SUBSTRACTOR full_substractor_3 (
    .A_BIT(TERM_0[2]), .B_BIT(TERM_1[2]), .BORROW_IN(full_substractor_2_borrow_out), .RESULT(RESULT[2]),
    .BORROW_OUT(full_substractor_3_borrow_out));
  FULL_SUBSTRACTOR full_substractor_4 (
    .A_BIT(TERM_0[3]), .B_BIT(TERM_1[3]), .BORROW_IN(full_substractor_3_borrow_out), .RESULT(RESULT[3]),
    .BORROW_OUT(BORROW_OUT));
endmodule

module MULTIPLIER (
  input  [3:0] TERM_0,
  input  [3:0] TERM_1,
  output [7:0] RESULT
);

  wire full_summator_1_carry_out, full_summator_2_carry_out, full_summator_2_result,
       full_summator_3_carry_out, full_summator_3_result, full_summator_4_carry_out, full_summator_4_result,
       full_summator_5_carry_out, full_summator_6_carry_out, full_summator_6_result,
       full_summator_7_carry_out, full_summator_7_result, full_summator_8_carry_out, full_summator_8_result,
       full_summator_9_carry_out, full_summator_10_carry_out, full_summator_11_carry_out,
       multiplier_2_result, multiplier_3_result, multiplier_4_result, multiplier_5_result,
       multiplier_6_result, multiplier_7_result, multiplier_8_result, multiplier_9_result,
       multiplier_10_result, multiplier_11_result, multiplier_12_result, multiplier_13_result,
       multiplier_14_result, multiplier_15_result, multiplier_16_result;

  \Примитивы_MULTIPLIER  multiplier_1 (.A_BIT(TERM_1[0]), .B_BIT(TERM_0[0]), .RESULT(RESULT[0]));
  \Примитивы_MULTIPLIER  multiplier_2 (.A_BIT(TERM_1[0]), .B_BIT(TERM_0[1]), .RESULT(multiplier_2_result));
  \Примитивы_MULTIPLIER  multiplier_3 (.A_BIT(TERM_1[0]), .B_BIT(TERM_0[2]), .RESULT(multiplier_3_result));
  \Примитивы_MULTIPLIER  multiplier_4 (.A_BIT(TERM_1[0]), .B_BIT(TERM_0[3]), .RESULT(multiplier_4_result));
  \Примитивы_MULTIPLIER  multiplier_5 (.A_BIT(TERM_1[1]), .B_BIT(TERM_0[0]), .RESULT(multiplier_5_result));
  \Примитивы_MULTIPLIER  multiplier_6 (.A_BIT(TERM_1[1]), .B_BIT(TERM_0[1]), .RESULT(multiplier_6_result));
  \Примитивы_MULTIPLIER  multiplier_7 (.A_BIT(TERM_1[1]), .B_BIT(TERM_0[2]), .RESULT(multiplier_7_result));
  \Примитивы_MULTIPLIER  multiplier_8 (.A_BIT(TERM_1[1]), .B_BIT(TERM_0[3]), .RESULT(multiplier_8_result));
  FULL_SUMMATOR full_summator_1 (
    .A_BIT(multiplier_2_result), .B_BIT(multiplier_5_result), .CARRY_IN(1'b0), .RESULT(RESULT[1]),
    .CARRY_OUT(full_summator_1_carry_out));
  FULL_SUMMATOR full_summator_2 (
    .A_BIT(multiplier_3_result), .B_BIT(multiplier_6_result), .CARRY_IN(full_summator_1_carry_out),
    .RESULT(full_summator_2_result), .CARRY_OUT(full_summator_2_carry_out));
  FULL_SUMMATOR full_summator_3 (
    .A_BIT(multiplier_4_result), .B_BIT(multiplier_7_result), .CARRY_IN(full_summator_2_carry_out),
    .RESULT(full_summator_3_result), .CARRY_OUT(full_summator_3_carry_out));
  FULL_SUMMATOR full_summator_4 (
    .A_BIT(1'b0), .B_BIT(multiplier_8_result), .CARRY_IN(full_summator_3_carry_out),
    .RESULT(full_summator_4_result), .CARRY_OUT(full_summator_4_carry_out));
  \Примитивы_MULTIPLIER  multiplier_9 (.A_BIT(TERM_1[2]), .B_BIT(TERM_0[0]), .RESULT(multiplier_9_result));
  \Примитивы_MULTIPLIER  multiplier_10 (.A_BIT(TERM_1[2]), .B_BIT(TERM_0[1]), .RESULT(multiplier_10_result));
  \Примитивы_MULTIPLIER  multiplier_11 (.A_BIT(TERM_1[2]), .B_BIT(TERM_0[2]), .RESULT(multiplier_11_result));
  \Примитивы_MULTIPLIER  multiplier_12 (.A_BIT(TERM_1[2]), .B_BIT(TERM_0[3]), .RESULT(multiplier_12_result));
  FULL_SUMMATOR full_summator_5 (
    .A_BIT(full_summator_2_result), .B_BIT(multiplier_9_result), .CARRY_IN(1'b0), .RESULT(RESULT[2]),
    .CARRY_OUT(full_summator_5_carry_out));
  FULL_SUMMATOR full_summator_6 (
    .A_BIT(full_summator_3_result), .B_BIT(multiplier_10_result), .CARRY_IN(full_summator_5_carry_out),
    .RESULT(full_summator_6_result), .CARRY_OUT(full_summator_6_carry_out));
  FULL_SUMMATOR full_summator_7 (
    .A_BIT(full_summator_4_result), .B_BIT(multiplier_11_result), .CARRY_IN(full_summator_6_carry_out),
    .RESULT(full_summator_7_result), .CARRY_OUT(full_summator_7_carry_out));
  FULL_SUMMATOR full_summator_8 (
    .A_BIT(full_summator_4_carry_out), .B_BIT(multiplier_12_result), .CARRY_IN(full_summator_7_carry_out),
    .RESULT(full_summator_8_result), .CARRY_OUT(full_summator_8_carry_out));
  \Примитивы_MULTIPLIER  multiplier_13 (.A_BIT(TERM_1[3]), .B_BIT(TERM_0[0]), .RESULT(multiplier_13_result));
  \Примитивы_MULTIPLIER  multiplier_14 (.A_BIT(TERM_1[3]), .B_BIT(TERM_0[1]), .RESULT(multiplier_14_result));
  \Примитивы_MULTIPLIER  multiplier_15 (.A_BIT(TERM_1[3]), .B_BIT(TERM_0[2]), .RESULT(multiplier_15_result));
  \Примитивы_MULTIPLIER  multiplier_16 (.A_BIT(TERM_1[3]), .B_BIT(TERM_0[3]), .RESULT(multiplier_16_result));
  FULL_SUMMATOR full_summator_9 (
    .A_BIT(full_summator_6_result), .B_BIT(multiplier_13_result), .CARRY_IN(1'b0), .RESULT(RESULT[3]),
    .CARRY_OUT(full_summator_9_carry_out));
  FULL_SUMMATOR full_summator_10 (
    .A_BIT(full_summator_7_result), .B_BIT(multiplier_14_result), .CARRY_IN(full_summator_9_carry_out),
    .RESULT(RESULT[4]), .CARRY_OUT(full_summator_10_carry_out));
  FULL_SUMMATOR full_summator_11 (
    .A_BIT(full_summator_8_result), .B_BIT(multiplier_15_result), .CARRY_IN(full_summator_10_carry_out),
    .RESULT(RESULT[5]), .CARRY_OUT(full_summator_11_carry_out));
  FULL_SUMMATOR full_summator_12 (
    .A_BIT(full_summator_8_carry_out), .B_BIT(multiplier_16_result), .CARRY_IN(full_summator_11_carry_out),
    .RESULT(RESULT[6]), .CARRY_OUT(RESULT[7]));
endmodule

module DIVIDER (
  input  [3:0] TERM_0,
  input  [3:0] TERM_1,
  output [3:0] QUOTIENT,
  output [3:0] REMAINDER,
  output ERROR
);

  wire and_1_out, and_2_out, full_summator_1_carry_out, full_summator_1_result, full_summator_2_carry_out,
       full_summator_2_result, full_summator_3_carry_out, full_summator_3_result, full_summator_4_carry_out,
       full_summator_4_result, full_summator_5_carry_out, full_summator_5_result, full_summator_6_carry_out,
       full_summator_6_result, full_summator_7_carry_out, full_summator_7_result, full_summator_8_carry_out,
       full_summator_8_result, full_summator_9_carry_out, full_summator_9_result, full_summator_10_result,
       full_summator_11_carry_out, full_summator_11_result, full_summator_12_carry_out,
       full_summator_12_result, full_summator_13_result, full_summator_14_carry_out, full_summator_14_result,
       full_summator_15_result, full_summator_16_result, muxer_2_to_1_1_out, muxer_2_to_1_2_out,
       muxer_2_to_1_3_out, muxer_2_to_1_4_out, muxer_2_to_1_5_out, muxer_2_to_1_6_out, muxer_2_to_1_7_out,
       muxer_2_to_1_8_out, muxer_2_to_1_9_out, muxer_2_to_1_11_out, muxer_2_to_1_12_out, muxer_2_to_1_14_out,
       muxer_2_to_1_16_out, muxer_2_to_1_17_out, muxer_2_to_1_18_out, muxer_2_to_1_19_out,
       muxer_2_to_1_20_out, not_1_out, not_2_out, not_3_out, not_4_out, not_5_out, not_6_out, not_7_out,
       not_8_out, not_9_out, not_10_out, or_1_out;

  nor nor_1 (ERROR, TERM_1[0], TERM_1[1], TERM_1[2], TERM_1[3]);
  not not_1 (not_1_out, TERM_1[3]);
  not not_2 (not_2_out, TERM_1[2]);
  not not_3 (not_3_out, TERM_1[1]);
  not not_4 (not_4_out, TERM_1[0]);
  FULL_SUMMATOR full_summator_1 (
    .A_BIT(not_4_out), .B_BIT(TERM_0[3]), .CARRY_IN(1'b1), .RESULT(full_summator_1_result),
    .CARRY_OUT(full_summator_1_carry_out));
  MUXER_2_TO_1 muxer_2_to_1_1 (
    .IN_0(full_summator_1_result), .IN_1(TERM_0[3]), .OUT(muxer_2_to_1_1_out),
    .SELECT(full_summator_10_result));
  FULL_SUMMATOR full_summator_2 (
    .A_BIT(not_4_out), .B_BIT(TERM_0[2]), .CARRY_IN(1'b1), .RESULT(full_summator_2_result),
    .CARRY_OUT(full_summator_2_carry_out));
  FULL_SUMMATOR full_summator_3 (
    .A_BIT(not_3_out), .B_BIT(1'b0), .CARRY_IN(full_summator_1_carry_out), .RESULT(full_summator_3_result),
    .CARRY_OUT(full_summator_3_carry_out));
  MUXER_2_TO_1 muxer_2_to_1_2 (
    .IN_0(full_summator_2_result), .IN_1(TERM_0[2]), .OUT(muxer_2_to_1_2_out),
    .SELECT(full_summator_13_result));
  MUXER_2_TO_1 muxer_2_to_1_3 (
    .IN_0(full_summator_3_result), .IN_1(1'b0), .OUT(muxer_2_to_1_3_out), .SELECT(full_summator_10_result));
  FULL_SUMMATOR full_summator_4 (
    .A_BIT(not_4_out), .B_BIT(TERM_0[1]), .CARRY_IN(1'b1), .RESULT(full_summator_4_result),
    .CARRY_OUT(full_summator_4_carry_out));
  FULL_SUMMATOR full_summator_5 (
    .A_BIT(not_3_out), .B_BIT(muxer_2_to_1_1_out), .CARRY_IN(full_summator_2_carry_out),
    .RESULT(full_summator_5_result), .CARRY_OUT(full_summator_5_carry_out));
  MUXER_2_TO_1 muxer_2_to_1_4 (
    .IN_0(full_summator_4_result), .IN_1(TERM_0[1]), .OUT(muxer_2_to_1_4_out),
    .SELECT(full_summator_15_result));
  FULL_SUMMATOR full_summator_6 (
    .A_BIT(not_2_out), .B_BIT(1'b0), .CARRY_IN(full_summator_3_carry_out), .RESULT(full_summator_6_result),
    .CARRY_OUT(full_summator_6_carry_out));
  MUXER_2_TO_1 muxer_2_to_1_5 (
    .IN_0(full_summator_5_result), .IN_1(muxer_2_to_1_1_out), .OUT(muxer_2_to_1_5_out),
    .SELECT(full_summator_13_result));
  FULL_SUMMATOR full_summator_7 (
    .A_BIT(not_4_out), .B_BIT(TERM_0[0]), .CARRY_IN(1'b1), .RESULT(full_summator_7_result),
    .CARRY_OUT(full_summator_7_carry_out));
  MUXER_2_TO_1 muxer_2_to_1_6 (
    .IN_0(full_summator_6_result), .IN_1(1'b0), .OUT(muxer_2_to_1_6_out), .SELECT(full_summator_10_result));
  FULL_SUMMATOR full_summator_8 (
    .A_BIT(not_3_out), .B_BIT(muxer_2_to_1_2_out), .CARRY_IN(full_summator_4_carry_out),
    .RESULT(full_summator_8_result), .CARRY_OUT(full_summator_8_carry_out));
  MUXER_2_TO_1 muxer_2_to_1_7 (
    .IN_0(full_summator_7_result), .IN_1(TERM_0[0]), .OUT(muxer_2_to_1_7_out),
    .SELECT(full_summator_16_result));
  FULL_SUMMATOR full_summator_9 (
    .A_BIT(not_2_out), .B_BIT(muxer_2_to_1_3_out), .CARRY_IN(full_summator_5_carry_out),
    .RESULT(full_summator_9_result), .CARRY_OUT(full_summator_9_carry_out));
  MUXER_2_TO_1 muxer_2_to_1_8 (
    .IN_0(full_summator_8_result), .IN_1(muxer_2_to_1_2_out), .OUT(muxer_2_to_1_8_out),
    .SELECT(full_summator_15_result));
  FULL_SUMMATOR full_summator_10 (
    .A_BIT(not_1_out), .B_BIT(1'b0), .CARRY_IN(full_summator_6_carry_out), .RESULT(full_summator_10_result));  // open: CARRY_OUT
  MUXER_2_TO_1 muxer_2_to_1_9 (
    .IN_0(full_summator_9_result), .IN_1(muxer_2_to_1_3_out), .OUT(muxer_2_to_1_9_out),
    .SELECT(full_summator_13_result));
  FULL_SUMMATOR full_summator_11 (
    .A_BIT(not_3_out), .B_BIT(muxer_2_to_1_4_out), .CARRY_IN(full_summator_7_carry_out),
    .RESULT(full_summator_11_result), .CARRY_OUT(full_summator_11_carry_out));
  MUXER_2_TO_1 muxer_2_to_1_10 (
    .IN_0(full_summator_10_result), .IN_1(1'b0), .SELECT(full_summator_10_result));  // open: OUT
  FULL_SUMMATOR full_summator_12 (
    .A_BIT(not_2_out), .B_BIT(muxer_2_to_1_5_out), .CARRY_IN(full_summator_8_carry_out),
    .RESULT(full_summator_12_result), .CARRY_OUT(full_summator_12_carry_out));
  MUXER_2_TO_1 muxer_2_to_1_11 (
    .IN_0(full_summator_11_result), .IN_1(muxer_2_to_1_4_out), .OUT(muxer_2_to_1_11_out),
    .SELECT(full_summator_16_result));
  not not_5 (not_5_out, full_summator_10_result);
  FULL_SUMMATOR full_summator_13 (
    .A_BIT(not_1_out), .B_BIT(muxer_2_to_1_6_out), .CARRY_IN(full_summator_9_carry_out),
    .RESULT(full_summator_13_result));  // open: CARRY_OUT
  MUXER_2_TO_1 muxer_2_to_1_12 (
    .IN_0(full_summator_12_result), .IN_1(muxer_2_to_1_5_out), .OUT(muxer_2_to_1_12_out),
    .SELECT(full_summator_15_result));
  MUXER_2_TO_1 muxer_2_to_1_13 (
    .IN_0(full_summator_13_result), .IN_1(muxer_2_to_1_6_out), .SELECT(full_summator_13_result));  // open: OUT
  FULL_SUMMATOR full_summator_14 (
    .A_BIT(not_2_out), .B_BIT(muxer_2_to_1_8_out), .CARRY_IN(full_summator_11_carry_out),
    .RESULT(full_summator_14_result), .CARRY_OUT(full_summator_14_carry_out));
  not not_6 (not_6_out, full_summator_13_result);
  FULL_SUMMATOR full_summator_15 (
    .A_BIT(not_1_out), .B_BIT(muxer_2_to_1_9_out), .CARRY_IN(full_summator_12_carry_out),
    .RESULT(full_summator_15_result));  // open: CARRY_OUT
  MUXER_2_TO_1 muxer_2_to_1_14 (
    .IN_0(full_summator_14_result), .IN_1(muxer_2_to_1_8_out), .OUT(muxer_2_to_1_14_out),
    .SELECT(full_summator_16_result));
  MUXER_2_TO_1 muxer_2_to_1_15 (
    .IN_0(full_summator_15_result), .IN_1(muxer_2_to_1_9_out), .SELECT(full_summator_15_result));  // open: OUT
  not not_7 (not_7_out, full_summator_15_result);
  FULL_SUMMATOR full_summator_16 (
    .A_BIT(not_1_out), .B_BIT(muxer_2_to_1_12_out), .CARRY_IN(full_summator_14_carry_out),
    .RESULT(full_summator_16_result));  // open: CARRY_OUT
  MUXER_2_TO_1 muxer_2_to_1_16 (
    .IN_0(full_summator_16_result), .IN_1(muxer_2_to_1_12_out), .OUT(muxer_2_to_1_16_out),
    .SELECT(full_summator_16_result));
  not not_8 (not_8_out, full_summator_16_result);
  or or_1 (or_1_out, not_1_out, not_2_out, not_3_out, not_4_out);
  and and_1 (and_1_out, TERM_0[3], TERM_0[2], TERM_0[1], TERM_0[0]);
  not not_9 (not_9_out, or_1_out);
  MUXER_2_TO_1 muxer_2_to_1_17 (.IN_0(TERM_0[3]), .IN_1(not_5_out), .OUT(muxer_2_to_1_17_out), .SELECT(or_1_out));
  MUXER_2_TO_1 muxer_2_to_1_18 (.IN_0(TERM_0[2]), .IN_1(not_6_out), .OUT(muxer_2_to_1_18_out), .SELECT(or_1_out));
  MUXER_2_TO_1 muxer_2_to_1_19 (.IN_0(TERM_0[1]), .IN_1(not_7_out), .OUT(muxer_2_to_1_19_out), .SELECT(or_1_out));
  MUXER_2_TO_1 muxer_2_to_1_20 (.IN_0(TERM_0[0]), .IN_1(not_8_out), .OUT(muxer_2_to_1_20_out), .SELECT(or_1_out));
  and and_2 (and_2_out, and_1_out, not_9_out);
  not not_10 (not_10_out, and_2_out);
  MUXER_2_TO_1 muxer_2_to_1_21 (.IN_0(1'b0), .IN_1(muxer_2_to_1_16_out), .OUT(REMAINDER[3]), .SELECT(or_1_out));
  MUXER_2_TO_1 muxer_2_to_1_22 (.IN_0(1'b0), .IN_1(muxer_2_to_1_14_out), .OUT(REMAINDER[2]), .SELECT(or_1_out));
  MUXER_2_TO_1 muxer_2_to_1_23 (.IN_0(1'b0), .IN_1(muxer_2_to_1_11_out), .OUT(REMAINDER[1]), .SELECT(or_1_out));
  MUXER_2_TO_1 muxer_2_to_1_24 (.IN_0(1'b0), .IN_1(muxer_2_to_1_7_out), .OUT(REMAINDER[0]), .SELECT(or_1_out));
  MUXER_2_TO_1 muxer_2_to_1_25 (.IN_0(1'b0), .IN_1(muxer_2_to_1_17_out), .OUT(QUOTIENT[3]), .SELECT(not_10_out));
  MUXER_2_TO_1 muxer_2_to_1_26 (.IN_0(1'b0), .IN_1(muxer_2_to_1_18_out), .OUT(QUOTIENT[2]), .SELECT(not_10_out));
  MUXER_2_TO_1 muxer_2_to_1_27 (.IN_0(1'b0), .IN_1(muxer_2_to_1_19_out), .OUT(QUOTIENT[1]), .SELECT(not_10_out));
  MUXER_2_TO_1 muxer_2_to_1_28 (.IN_0(1'b1), .IN_1(muxer_2_to_1_20_out), .OUT(QUOTIENT[0]), .SELECT(not_10_out));
endmodule

module COMPARATOR (
  input  [3:0] TERM_0,
  input  [3:0] TERM_1,
  output MORE,
  output EQUAL,
  output LESS
);

  wire and_1_out, and_2_out, and_3_out, and_4_out, and_5_out, and_6_out, comparator_1_equal,
       comparator_1_less, comparator_1_more, comparator_2_equal, comparator_2_less, comparator_2_more,
       comparator_3_equal, comparator_3_less, comparator_3_more, comparator_4_equal, comparator_4_less,
       comparator_4_more;

  \Примитивы_COMPARATOR  comparator_1 (
    .A_BIT(TERM_0[0]), .B_BIT(TERM_1[0]), .MORE(comparator_1_more), .EQUAL(comparator_1_equal),
    .LESS(comparator_1_less));
  \Примитивы_COMPARATOR  comparator_2 (
    .A_BIT(TERM_0[1]), .B_BIT(TERM_1[1]), .MORE(comparator_2_more), .EQUAL(comparator_2_equal),
    .LESS(comparator_2_less));
  \Примитивы_COMPARATOR  comparator_3 (
    .A_BIT(TERM_0[2]), .B_BIT(TERM_1[2]), .MORE(comparator_3_more), .EQUAL(comparator_3_equal),
    .LESS(comparator_3_less));
  \Примитивы_COMPARATOR  comparator_4 (
    .A_BIT(TERM_0[3]), .B_BIT(TERM_1[3]), .MORE(comparator_4_more), .EQUAL(comparator_4_equal),
    .LESS(comparator_4_less));
  and and_1 (and_1_out, comparator_3_more, comparator_4_equal);
  and and_2 (and_2_out, comparator_2_more, comparator_4_equal, comparator_3_equal);
  and and_3 (and_3_out, comparator_1_more, comparator_4_equal, comparator_3_equal, comparator_2_equal);
  and and_4 (and_4_out, comparator_2_equal, comparator_3_equal, comparator_4_equal, comparator_1_less);
  and and_5 (and_5_out, comparator_3_equal, comparator_4_equal, comparator_2_less);
  and and_6 (and_6_out, comparator_4_equal, comparator_3_less);
  or or_1 (MORE, comparator_4_more, and_1_out, and_2_out, and_3_out);
  and and_7 (EQUAL, comparator_1_equal, comparator_2_equal, comparator_3_equal, comparator_4_equal);
  or or_2 (LESS, and_4_out, and_5_out, and_6_out, comparator_4_less);
endmodule

module REGISTER (
  input  [3:0] DATA,
  input  CLOCK,
  output [3:0] RESULT
);

  D_TRIGGER d_trigger_1 (.DATA(DATA[0]), .CLK(CLOCK), .RESULT(RESULT[0]));  // open: NOT_RESULT
  D_TRIGGER d_trigger_2 (.DATA(DATA[1]), .CLK(CLOCK), .RESULT(RESULT[1]));  // open: NOT_RESULT
  D_TRIGGER d_trigger_3 (.DATA(DATA[2]), .CLK(CLOCK), .RESULT(RESULT[2]));  // open: NOT_RESULT
  D_TRIGGER d_trigger_4 (.DATA(DATA[3]), .CLK(CLOCK), .RESULT(RESULT[3]));  // open: NOT_RESULT
endmodule

module SHIFTER (
  input  [3:0] DATA,
  input  LEFT,
  input  LOOP,
  output [3:0] RESULT
);

  wire and_1_out, and_2_out;

  and and_1 (and_1_out, DATA[0], LOOP);
  and and_2 (and_2_out, DATA[3], LOOP);
  MUXER_2_TO_1 muxer_2_to_1_1 (.IN_0(DATA[1]), .IN_1(and_2_out), .OUT(RESULT[0]), .SELECT(LEFT));
  MUXER_2_TO_1 muxer_2_to_1_2 (.IN_0(DATA[2]), .IN_1(DATA[0]), .OUT(RESULT[1]), .SELECT(LEFT));
  MUXER_2_TO_1 muxer_2_to_1_3 (.IN_0(DATA[3]), .IN_1(DATA[1]), .OUT(RESULT[2]), .SELECT(LEFT));
  MUXER_2_TO_1 muxer_2_to_1_4 (.IN_0(and_1_out), .IN_1(DATA[2]), .OUT(RESULT[3]), .SELECT(LEFT));
endmodule
